// Logisim project domaci_zadatak_2.circ as structural Verilog: 2 circuits, main circuit kolo
module kolo (
  input  x1,
  input  x2,
  input  x3,
  input  x4,
  input  x5,
  output y
);

  wire and_1_out, and_2_out, and_4_out, not_1_out, not_2_out, not_3_out;

  not not_1 (not_1_out, x2);
  and and_1 (and_1_out, x1, not_1_out);
  not not_2 (not_2_out, x3);
  not not_3 (not_3_out, x4);
  and and_2 (and_2_out, and_1_out, not_2_out);
  and and_3 (y, and_2_out, and_4_out);
  and and_4 (and_4_out, not_3_out, x5);
endmodule

module domaci_zadatak (
  input  x1,
  input  x2,
  input  x3,
  input  x4,
  input  x5,
  output y
);

  wire nor_1_out, nor_2_out, nor_3_out, nor_4_out, nor_5_out, nor_6_out, nor_7_out, nor_8_out;

  nor nor_1 (nor_1_out, x1, x1);
  nor nor_2 (nor_2_out, x5, x5);
  nor nor_3 (nor_3_out, nor_1_out, x2);
  nor nor_4 (nor_4_out, x4, nor_2_out);
  nor nor_5 (nor_5_out, nor_3_out, nor_3_out);
  nor nor_6 (nor_6_out, nor_4_out, nor_4_out);
  nor nor_7 (nor_7_out, nor_5_out, x3);
  nor nor_8 (nor_8_out, nor_7_out, nor_7_out);
  nor nor_9 (y, nor_8_out, nor_6_out);

  // Notes on the sheet:
  //   16
  //   8
  //   4
  //   2
  //   1
  //   datum rodjenja: 19.07
  //   zbir cifara: 1+9+0+7=17
endmodule
